// Logisim project first.circ as structural Verilog: 1 circuit, main circuit main
module main (
  input  Floor_1,
  input  Floor_2,
  input  Floor_3,
  input  Floor_4,
  input  Floor_5,
  input  Floor_6,
  input  Floor_7,
  input  Reset
);

  wire and_1_p1, and_2_p1, comparator_1_eq, counter_1_p1, d_ff_1_p1, d_ff_1_p2, d_ff_2_p1, decoder_1_p1,
       n7_segment_display_1_p1, priority_encoder_1_p1, priority_encoder_1_p2, priority_encoder_1_p4,
       undriven, undriven_2, undriven_3, undriven_4, undriven_5, undriven_6;

  // Priority_Encoder priority_encoder_1: pin names not known; wires that end beside it: priority_encoder_1_p1, priority_encoder_1_p2, priority_encoder_1_p1, priority_encoder_1_p4, priority_encoder_1_p2
  // D_Flip_Flop d_ff_1: pin names not known; wires that end beside it: d_ff_1_p1, d_ff_1_p2
  // D_Flip_Flop d_ff_2: pin names not known; wires that end beside it: d_ff_2_p1, d_ff_1_p1
  // D_Flip_Flop d_ff_3: pin names not known; wires that end beside it: d_ff_2_p1
  Comparator comparator_1 (.eq(comparator_1_eq));  // open: a, b, gt, lt
  // AND_Gate and_1: pin names not known; wires that end beside it: and_1_p1
  // AND_Gate and_2: pin names not known; wires that end beside it: and_2_p1
  // Counter counter_1: pin names not known; wires that end beside it: counter_1_p1, counter_1_p1
  // Decoder decoder_1: pin names not known; wires that end beside it: decoder_1_p1
  // _7_Segment_Display 7_segment_display_1: pin names not known; wires that end beside it: n7_segment_display_1_p1
  LED led_1 (.in(undriven));
  LED led_2 (.in(undriven_2));
  LED led_3 (.in(undriven_3));
  LED led_4 (.in(decoder_1_p1));
  LED led_5 (.in(undriven_4));
  LED led_6 (.in(undriven_5));
  LED led_7 (.in(undriven_6));
endmodule
